# Fritzing sketch KoloBox (saved by Fritzing 0.9.3b)
breadboards: 1

parts:
  WeMos_D1_Mini1 = WeMos D1 Mini
  TP1 = TP4056 [chip_label=TP4056 package="DIP (Dual Inline) [THT]"]
  BAT1 = 18650 battery holder [package=battery-18650-kit]
  J1 = Piezo Speaker
  NEOPIXEL1 = Neopixel Strip -- White (60/m)

nets:
  N1: WeMos_D1_Mini1.3V3, NEOPIXEL1.DI
  N2: WeMos_D1_Mini1.D6, NEOPIXEL1.+5V
  N3: WeMos_D1_Mini1.G, J1.pin1, NEOPIXEL1.GND
  N4: TP1.pin4, BAT1.+
  N5: TP1.pin5, BAT1.-

custom parts:
  TP4056: A DIP stand-in part for whatever IC you want. With 6 pins on a 300mil dual inline package (DIP) footprint.
  18650 battery holder: 18650 Battery Holder
  Neopixel Strip -- White (60/m): Neopixel Strip, White, 60 pixels per meter.
